// Logisim project PiCPU.circ as structural Verilog: 1 circuit, main circuit main
module main (
);

  wire AC, C1, C2, clock_1_out, comparator_1_eq, comparator_2_eq, comparator_3_eq, comparator_4_eq,
       comparator_5_eq, comparator_6_eq, comparator_7_eq, comparator_8_eq, comparator_9_eq,
       ProgramCounter_carry, Reset, s_r_ff_1_q, s_r_ff_2_q, Stop;
  wire [3:0] SI_Counter_q;
  wire [7:0] Inst, OE, RS, WE;
  wire [15:0] bit_extender_1_out, CounterMemory_dout, multiplexer_1_out, ProgramData, SI;
  wire [23:0] ProgramCounter_q;

  Button button_1 (.out(Reset));
  S_R_Flip_Flop s_r_ff_1 (.S(1'b0), .R(1'b0), .clk(1'b0), .Q(s_r_ff_1_q), .reset(Stop), .preset(Reset));  // open: Qn
  Clock clock_1 (.out(clock_1_out));
  assign C1 = s_r_ff_1_q ? clock_1_out : 1'bz;  // Controlled_Buffer controlled_buffer_1
  Pull_Resistor pull_resistor_1 (.node(C1));
  S_R_Flip_Flop Waiting (.reset(Reset), .Qn(AC));  // open: S, R, clk, Q, preset
  Comparator #(.mode("unsigned")) comparator_1 (.a(WE), .b(8'h26), .eq(comparator_1_eq));  // open: gt, lt
  Comparator #(.mode("unsigned"), .width(16)) comparator_2 (.a(SI), .b(16'hff), .eq(comparator_2_eq));  // open: gt, lt
  Register ProgramSelector (
    .D(ProgramData[15:8]), .en(comparator_1_eq), .clk(C1), .Q(ProgramCounter_q[23:16]),
    .clr(ProgramCounter_carry));
  RAM #(.clearpin("true"), .dataWidth(16)) CounterMemory (
    .addr(ProgramCounter_q[23:16]), .we(comparator_2_eq), .oe(1'b1), .clk(C1), .din(ProgramCounter_q[15:0]),
    .dout(CounterMemory_dout), .clr(Reset));
  Comparator comparator_3 (.a({8{1'b0}}), .b(ProgramCounter_q[23:16]), .eq(comparator_3_eq));  // open: gt, lt
  and and_1 (Stop, comparator_3_eq, ProgramCounter_carry, ~Reset);  // AND_Gate
  assign bit_extender_1_out = {{8{1'b0}}, ProgramData[7:0]};  // Bit_Extender bit_extender_1
  S_R_Flip_Flop s_r_ff_2 (.S(comparator_4_eq), .R(1'b0), .clk(C1), .Q(s_r_ff_2_q), .reset(C2));  // open: Qn, preset
  Comparator #(.mode("unsigned"), .width(16)) comparator_4 (.a(SI), .b(16'hfe), .eq(comparator_4_eq));  // open: gt, lt
  Counter #(.max('hffff), .ongoal("stay"), .width(16)) ProgramCounter (
    .clr(Reset), .load(comparator_5_eq), .up(1'b1), .count(C2), .clk(C1), .D(multiplexer_1_out),
    .carry(ProgramCounter_carry), .Q(ProgramCounter_q[15:0]));
  Comparator #(.mode("unsigned")) comparator_5 (.a(WE), .b(8'h27), .eq(comparator_5_eq));  // open: gt, lt
  Multiplexer #(.width(16)) multiplexer_1 (
    .in0(CounterMemory_dout), .in1(bit_extender_1_out), .out(multiplexer_1_out), .sel(s_r_ff_2_q));
  ROM #(.addrWidth(24), .dataWidth(24)) Program (.addr(ProgramCounter_q), .data({Inst, ProgramData}));
  Counter #(.max('hf), .ongoal("stay"), .width(4)) SI_Counter (
    .clr(C2), .load(1'b0), .up(1'b1), .count(AC), .clk(C1), .Q(SI_Counter_q));  // open: D, carry
  Comparator #(.mode("unsigned"), .width(16)) comparator_6 (.a(SI), .b(16'h1), .eq(comparator_6_eq));  // open: gt, lt
  and and_2 (C2, comparator_6_eq, ~C1);  // AND_Gate
  ROM #(.addrWidth(12), .dataWidth(16)) rom_1 (.addr({Inst, SI_Counter_q}), .data(SI));
  Comparator comparator_7 (.a(SI[15:8]), .b(8'h1), .eq(comparator_7_eq));  // open: gt, lt
  Comparator comparator_8 (.a(SI[15:8]), .b(8'h2), .eq(comparator_8_eq));  // open: gt, lt
  Comparator comparator_9 (.a(SI[15:8]), .b(8'h2), .eq(comparator_9_eq));  // open: gt, lt
  Register u_WE (.D(SI[7:0]), .en(comparator_7_eq), .clk(C1), .Q(WE), .clr(C2));
  Register u_OE (.D(SI[7:0]), .en(comparator_8_eq), .clk(C1), .Q(OE), .clr(C2));
  assign RS = comparator_9_eq ? SI[7:0] : 8'bz;  // Controlled_Buffer controlled_buffer_2
  Pull_Resistor pull_resistor_2 (.node(RS));

  // Notes on the sheet:
  //   Clock
  //   Instructor Unit
  //   Subinstructor Unit
  //   Bus & Register Control
endmodule
